// Digital circuit alu_v2.dig as structural Verilog
module alu_v2 (
  input  [7:0] a_in,
  input  [7:0] b_in,
  input  clk,
  input  [2:0] OPSEL,
  input  rset,
  input  fi,
  input  fc,
  input  fo,
  input  [7:0] bus_in,
  input  [7:0] x_in,
  input  a_d,
  input  [2:0] x_d,
  output [7:0] flags_peek,
  output [7:0] bus_out
);

  wire alu_d, comparator_1_eq, comparator_1_gt, comparator_1_lt, opsel_add, opsel_cmp, opsel_sub, or_10_out,
       or_11_out, x_d_t;
  wire [1:0] add_1_c_o;
  wire [1:1] nor_1_out, nor_2_out;
  wire [2:2] lookuptable_1_out_2;
  wire [3:0] lookuptable_2_out;
  wire [7:0] a_d_flags, add_1_s, alu_d_flags, and_2_out, and_3_out, and_4_out, and_5_out, and_6_out,
       driver_6_out, lookuptable_1_out, or_7_out, or_8_out, or_9_out, sub_1_c_o, sub_1_s, x_d_flags;

  or or_1 (x_d_t, x_d[0], x_d[1], x_d[2]);
  nor nor_1 (nor_1_out[1], a_in[0], a_in[1], a_in[2], a_in[3], a_in[4], a_in[5], a_in[6], a_in[7]);
  Add #(.Bits(8)) add_1 (.a(a_in), .b(b_in), .c_i(1'b0), .s(add_1_s), .c_o(add_1_c_o[0]));
  Sub #(.Bits(8)) sub_1 (.a(a_in), .b(b_in), .c_i(1'b0), .s(sub_1_s), .c_o(sub_1_c_o[0]));
  Comparator #(.Bits(8)) comparator_1 (
    .a(a_in), .b(b_in), .gt(comparator_1_gt), .eq(comparator_1_eq), .lt(comparator_1_lt));
  BarrelShifter #(.Bits(8)) barrelshifter_1 (.in(a_in), .shift(4'b0001));  // open: out
  // And and_1 has open pins: In_1=a_in, In_2=b_in, out=open
  // Or or_2 has open pins: In_1=a_in, In_2=b_in, out=open
  // XOr xor_1 has open pins: In_1=a_in, In_2=b_in, out=open
  assign and_2_out = 8'h8a & flags_peek;  // And and_2, 8 bits wide
  assign a_d_flags = and_2_out | {a_in[7], {5{1'b0}}, nor_1_out[1], 1'b0};  // Or or_3, 8 bits wide
  Decoder #(.Selector_Bits(3)) decoder_1 (
    .sel(OPSEL), .out_1(opsel_add), .out_2(opsel_sub), .out_7(opsel_cmp));  // open: out_0, out_3, out_4, out_5, out_6
  or or_4 (alu_d, OPSEL[0], OPSEL[1], OPSEL[2]);
  LookUpTable #(.Bits(3)) lookuptable_1 (
    .in0(comparator_1_gt), .in1(comparator_1_eq), .in2(comparator_1_lt),
    .out({lookuptable_1_out_2[2], lookuptable_1_out[1:0]}));
  nor nor_2 (nor_2_out[1], x_in[0], x_in[1], x_in[2], x_in[3], x_in[4], x_in[5], x_in[6], x_in[7]);
  assign and_3_out = 8'h8a & flags_peek;  // And and_3, 8 bits wide
  assign bus_out = opsel_add ? add_1_s : 8'bz;  // Driver driver_1
  assign x_d_flags = and_3_out | {x_in[7], {5{1'b0}}, nor_2_out[1], 1'b0};  // Or or_5, 8 bits wide
  Comparator #(.Bits(8)) comparator_2 (.a(add_1_s), .b({8{1'b0}}), .eq(add_1_c_o[1]));  // open: gt, lt
  Comparator #(.Bits(8)) comparator_3 (.a(sub_1_s), .b({8{1'b0}}), .eq(sub_1_c_o[1]));  // open: gt, lt
  BitSelector #(.Selector_Bits(3)) bitselector_1 (.in(sub_1_s), .sel(3'b111), .out(sub_1_c_o[7]));
  assign and_4_out = flags_peek & 8'h7c;  // And and_4, 8 bits wide
  or or_6 (lookuptable_1_out[7], lookuptable_1_out_2[2], sub_1_s[7]);
  assign bus_out = opsel_sub ? sub_1_s : 8'bz;  // Driver driver_2
  assign and_5_out = flags_peek & 8'hfc;  // And and_5, 8 bits wide
  assign and_6_out = flags_peek & 8'h3d;  // And and_6, 8 bits wide
  assign or_7_out = and_5_out | {{6{1'b0}}, add_1_c_o};  // Or or_7, 8 bits wide
  assign or_8_out = and_6_out | {sub_1_c_o[7], {5{1'b0}}, sub_1_c_o[1:0]};  // Or or_8, 8 bits wide
  assign or_9_out = and_4_out | {lookuptable_1_out[7], {5{1'b0}}, lookuptable_1_out[1:0]};  // Or or_9, 8 bits wide
  assign alu_d_flags = opsel_cmp ? or_9_out : 8'bz;  // Driver driver_3
  assign alu_d_flags = opsel_add ? or_7_out : 8'bz;  // Driver driver_4
  assign alu_d_flags = opsel_sub ? or_8_out : 8'bz;  // Driver driver_5
  or or_10 (or_10_out, a_d, x_d_t, fi, alu_d);
  LookUpTable #(.Bits(4)) lookuptable_2 (.in0(fi), .in1(alu_d), .in2(a_d), .in3(x_d_t), .out(lookuptable_2_out));
  // Probe reg_set on or_10_out
  assign driver_6_out = lookuptable_2_out[3] ? x_d_flags : 8'bz;  // Driver driver_6
  assign driver_6_out = lookuptable_2_out[2] ? a_d_flags : 8'bz;  // Driver driver_7
  or or_11 (or_11_out, fc, rset);
  assign driver_6_out = lookuptable_2_out[1] ? alu_d_flags : 8'bz;  // Driver driver_8
  assign driver_6_out = lookuptable_2_out[0] ? bus_in : 8'bz;  // Driver driver_9
  register FLAGS (
    .bus_in(driver_6_out), .clk(clk), .rfb(or_10_out), .wtb(fo), .rset(or_11_out), .inc(1'b0),
    .bus_out(bus_out), .peek(flags_peek));  // open: cry
  // Probe reg_in on driver_6_out

  // Notes on the sheet:
  //   Compare Instruction Results
  //   Compare Result	N	Z	C
  //   A, X, or Y < Memory	*	0	0      0b*0000000
  //   A, X, or Y = Memory	0	1	1      0b00000011
  //   A, X, or Y > Memory	*	0	1      0b*0000001
  //   * The N flag will be bit 7 of A, X, or Y - Memory
  //   Flags Register BIts
  //   Carry
  //   Equal/Zero (one flag)
  //   Overflow
  //   negative
  //   7  bit  0
  //   ---- ----
  //   NV1B DIZC
  //   |||| ||||
  //   |||| |||+- Carry
  //   |||| ||+-- Zero
  //   |||| |+--- Interrupt Disable
  //   |||| +---- Decimal
  //   |||+------ (No CPU effect; see: the B flag)
  //   ||+------- (No CPU effect; always pushed as 1)
  //   |+-------- Overflow
  //   +--------- Negative
  //   contents of lookuptable_1 (hex, n*v repeats v):
  //   0,1,3
  //   contents of lookuptable_2 (hex, n*v repeats v):
  //   0,1,2,1,4,1,2,1,8,1,2,1,4,1,2,1
  //   Addition & Subtraction
  //   FLAGS:
  //   Set overflow if overflow during sub, which is if carry bit is set
  //   Set carry flag if carry is set on addition
  //   FIXME: Carry from current op fed back in and affects result of current op!
endmodule

/* Test case Compare:
clk OPSEL a_in b_in flags_peek
# A < B ; A = B ; A > B
C 7 0x00 0xff 0b00000000
C 7 0x02 0x02 0b00000011
C 7 0x0f 0x00 0b00000001

# Tests with negative results
C 7 0x81 0x83 0b10000000
C 7 0x81 0x81 0b00000011
# THIS TEST NOT WORKING
# C 7 0x8D 0x8F 0b10000011
C 7 0x8D 0x8F X
*/

/* Test case add sub:
clk fc OPSEL a_in b_in flags_peek bus_out
# NV1B DIZC
# Addition Tests
C 0 1 0x00 0xff 0b00000000 0xff
C 0 1 0xff 0x01 0b00000011 0x00
C 0 1 0xff 0x00 0b00000000 0xff

# Subtraction Tests
C 0 2 0x04 0x01 0b00000000 0x03
C 0 2 0x04 0x04 0b00000010 0x00
C 0 2 0x04 0x06 0b10000001 0xFE

# Clear test
C 1 0 0x00 0x00 X Z
# NO-OP test
C 0 0 0x12 0x34 0b00000000 Z
*/

/* Test case flags set logic:
clk fc fi OPSEL a_d x_d  bus_in a_in b_in  x_in    reg_set reg_in bus_out
# Test when nothing is set                                        
C   0  0  0     0   0    0xff   0x001 0x02 0x03    0       Z      X

# Test write to flags from bus
C   0  1  0     0   0    0xff   0x001 0x02 0x03    1       0xff   X
C   0  1  1     1   0    0xff   0x001 0x02 0x03    1       0xff   X
C   0  1  0     0   1    0xff   0x001 0x02 0x03    1       0xff   X

# Clear reg for next test
C   1  0  0     0   0    0xff   0x001 0x02 0x03    0       Z      X
C   1  0  0     0   0    0xff   0x001 0x02 0x03    0       Z      X
# Test Math Op
C   0  0  1     0   0    0xff   0x01 0xff 0x03     1       0x03   X
C   0  0  1     0   0    0xff   0x01 0xf0 0x03     1       0x00   X

# Clear reg for next test
C   1  0  0     0   0    0xff   0x001 0x02 0x03    0       Z      X
# Test accum Op
C   0  0  0     1   0    0xff   0x00 0x02 0x03    1       0x02    X
C   0  0  0     1   1    0xff   0x00 0x02 0x03    1       0x02    X

# Clear reg for next test
C   1  0  0     0   0    0xff   0x001 0x02 0x03    0       Z      X
# test X Op
C   0  0  0     0   1    0xff   0x00 0x02 0xff    1       0x80    X
C   0  0  0     0   1    0xff   0x00 0x02 0xff    1       0x80    X
*/
