// Digital circuit digital_sap1p.dig as structural Verilog
module digital_sap1p (
  input  clk,
  output [7:0] databus,
  output [7:0] out_3,
  output [7:0] out_4,
  output [7:0] out_5,
  output out_6,
  output [15:0] addrbus,
  output [7:0] out_8,
  output [7:0] out_9,
  output [7:0] out_10,
  output out_11,
  output [11:0] out_12,
  output [31:0] out_13,
  output [7:0] out_14,
  output [7:0] out_15
);

  wire and_1_out, clk_t, coldstart_q, decoder_2_out_0, decoder_2_out_2, decoder_2_out_3, Man_Auto_out,
       MRH_cry, mrho, MRL_cry, mrlo, PCL_cry, pco, rs_ff_as_1_q, rset, spo, t_ff_1_q, Tick_out, zpo;
  wire [3:0] mmio_1_p11, mmio_1_p12;
  wire [8:0] driver_1_out;

  T_FF t_ff_1 (.T(Man_Auto_out), .C(Man_Auto_out), .Q(t_ff_1_q), .nQ(out_11));
  Button Man_Auto (.out(Man_Auto_out));
  Button Tick (.out(Tick_out));
  and and_1 (and_1_out, t_ff_1_q, clk);
  or or_1 (clk_t, Tick_out, and_1_out);
  Reset reset_1 ();  // open: out
  Button button_1 (.out(rset));
  register IR (
    .bus_in(databus), .clk(clk_t), .rfb(out_13[10]), .wtb(1'b0), .rset(rset), .inc(1'b0), .peek(out_12[11:4]));  // open: bus_out, cry
  Counter #(.Bits(4)) counter_1 (.en(1'b1), .C(clk_t), .clr(out_13[7]), .out(out_12[3:0]));  // open: ovf
  ROM #(.AddrBits(12), .Bits(32)) rom_1 (.A(out_12), .sel(1'b1), .D(out_13));
  alu_v2 alu_v2_1 ();  // open: a_in, b_in, clk, OPSEL, rset, fi, fc, fo, bus_in, flags_peek, sub_peek, bus_out
  RS_FF_AS rs_ff_as_1 (.S(clk_t), .R(rset), .Q(rs_ff_as_1_q));  // open: nQ
  register REG_A (
    .bus_in(databus), .clk(clk_t), .rfb(out_13[3]), .wtb(out_13[4]), .rset(rset), .inc(1'b0),
    .bus_out(databus), .peek(out_3));  // open: cry
  register REG_B (
    .bus_in(databus), .clk(clk_t), .rfb(out_13[13]), .wtb(out_13[14]), .rset(rset), .inc(1'b0),
    .bus_out(databus), .peek(out_4));  // open: cry
  LED led_1 (.in(out_13[0]));
  LED led_2 (.in(out_13[2]));
  LED led_3 (.in(out_13[1]));
  Monoflop #(.timerDelay(2)) coldstart (.C(rs_ff_as_1_q), .R(1'b0), .Q(coldstart_q));  // open: nQ
  LED led_4 (.in(out_13[4]));
  LED led_5 (.in(out_13[6]));
  LED led_6 (.in(out_13[3]));
  LED led_7 (.in(out_13[5]));
  pc_controller PC_CONT ();  // open: PC_sel, bus_in, flags_in, clk, rset, cold_ena, pcli, pchi, pcl_bo, pch_bo
  assign driver_1_out[8] = ~coldstart_q ? out_13[2] : 1'bz;  // DriverInvSel driverinvsel_1
  assign driver_1_out = coldstart_q ? 9'h1fc : 9'bz;  // Driver driver_1
  alu ALU (.a_in(out_3), .b_in(out_4), .ena(out_13[6]), .sub(1'b0), .peek(out_5), .c_o(out_6), .bus_out(databus));
  LED led_8 (.in(out_13[8]));
  LED led_9 (.in(out_13[10]));
  LED led_10 (.in(out_13[7]));
  LED led_11 (.in(out_13[9]));
  assign driver_1_out[7:0] = ~coldstart_q ? databus : 8'bz;  // DriverInvSel driverinvsel_2
  LED led_12 (.in(out_13[12]));
  LED led_13 (.in(out_13[14]));
  LED led_14 (.in(out_13[11]));
  LED led_15 (.in(out_13[13]));
  register PCH (
    .bus_in(databus), .clk(clk_t), .rfb(1'b0), .wtb(pco), .rset(rset), .inc(PCL_cry), .bus_out(addrbus[15:8]));  // open: peek, cry
  register PCL (
    .bus_in(driver_1_out[7:0]), .clk(clk_t), .rfb(driver_1_out[8]), .wtb(pco), .rset(rset), .inc(out_13[1]),
    .bus_out(addrbus[7:0]), .peek(out_8), .cry(PCL_cry));
  register MRH (
    .bus_in(databus), .clk(clk_t), .rfb(1'b0), .wtb(mrho), .rset(rset), .inc(1'b0), .bus_out(addrbus[15:8]),
    .peek(out_9), .cry(MRH_cry));
  register MRL (
    .bus_in(databus), .clk(clk_t), .rfb(out_13[5]), .wtb(mrlo), .rset(rset), .inc(1'b0),
    .bus_out(addrbus[7:0]), .peek(out_10), .cry(MRL_cry));
  Decoder #(.Selector_Bits(2)) decoder_1 (.sel(out_13[9:8]), .out_0(pco), .out_1(mrho), .out_2(zpo), .out_3(spo));
  or or_2 (mrlo, mrho, zpo, spo);
  assign addrbus[15:8] = zpo ? 8'h1 : 8'bz;  // Driver driver_2
  Driver #(.Bits(8)) driver_3 (.in({8{1'b0}}), .en(spo));  // open: out
  Decoder #(.Selector_Bits(2)) decoder_2 (
    .sel(addrbus[7:6]), .out_0(decoder_2_out_0), .out_2(decoder_2_out_2), .out_3(decoder_2_out_3));  // open: out_1
  RAMDualPort #(.AddrBits(6), .Bits(8)) ramdualport_1 (
    .A(addrbus[5:0]), .Din(databus), .str(out_13[12]), .C(clk_t), .ld(decoder_2_out_0), .D(out_14));
  // mmio mmio_1: pin names not known; wires that end beside it: addrbus[5:0], addrbus[5:0], databus, out_13[12], clk_t, decoder_2_out_2, rset, addrbus[5:0], {6{1'b0}}, out_14, mmio_1_p11, mmio_1_p12
  ROM #(.AddrBits(6), .Bits(8)) rom_2 (.A(addrbus[5:0]), .sel(decoder_2_out_3), .D(out_14));
  assign databus = out_13[11] ? out_14 : 8'bz;  // Driver driver_4
  Seven_Seg_Hex seven_seg_hex_1 (.d(mmio_1_p11), .dp(1'b0));
  Seven_Seg_Hex seven_seg_hex_2 (.d(mmio_1_p12), .dp(1'b0));

  assign out_15 = out_12[11:4];
  // also tied to GND on the sheet: {MRH_cry, MRL_cry}

  // Other names for the same wires on the sheet: abus[15:0] = addrbus; dbus[7:0] = databus; hlt = out_13[0];
  //   ci = out_13[1]; pcli = out_13[2]; ai = out_13[3]; ao = out_13[4]; mrli = out_13[5]; aluo = out_13[6];
  //   end = out_13[7]; ms1 = out_13[8]; ms2 = out_13[9]; iri = out_13[10]; mo = out_13[11]; mi = out_13[12];
  //   bi = out_13[13]; bo = out_13[14]

  // Notes on the sheet:
  //   clk: Hz: 50
  //   addrbus: The Address Bus
  //   contents of rom_1 (hex, n*v repeats v):
  //   ff,88
  //   0-63 RAM
  //   128-191 IO
  //   192-255 ROM
  //   contents of rom_2 (hex, n*v repeats v):
  //   127*0,10
endmodule
