// Digital circuit mem_cont.dig as structural Verilog
module mem_cont (
  input  [7:0] mrh,
  input  [7:0] mrl,
  input  [7:0] xreg,
  input  [7:0] sp,
  input  ms1,
  input  ms2,
  input  [15:0] pca,
  output [15:0] abus
);

  wire [15:0] add_1_s;

  Add #(.Bits(16)) add_1 (.a({mrh, mrl}), .b({{8{1'b0}}, xreg}), .c_i(1'b0), .s(add_1_s));  // open: c_o
  Multiplexer #(.Bits(16), .Selector_Bits(2)) multiplexer_1 (
    .sel({ms2, ms1}), .in_0(pca), .in_1({mrh, mrl}), .in_2(add_1_s), .in_3({8'h1, sp}), .out(abus));

  // Notes on the sheet:
  //   MSPC = 0b00 << 8 # Program Counter selected for addr bus
  //   MSMR = 0b01 << 8 # Full Mem register selected for addr bus
  //   MSXI = 0b10 << 8 # MRL/MRH added to value of X register. X Indexed ops
  //   MSSP = 0b11 << 8 # Stack Pointer low and value 0x01 high written to bus, Stack ops
endmodule

/* Test case:
ms2 ms1 mrh  mrl  xreg sp   pca    abus   
0   0   0x10 0x05 0x02 0x03 0x1002 0x1002 
0   1   0x10 0x05 0x02 0x03 0x1002 0x1005 
1   0   0x10 0x05 0x02 0x03 0x1002 0x1007 
1   1   0x10 0x05 0x02 0x03 0x1002 0x0103 
*/
