// Digital circuit mmio_v2.dig as structural Verilog
module mmio_v2 (
  input  [7:0] bus_in,
  input  rfb,
  input  clk,
  input  wtb,
  input  rset,
  input  [5:0] addr_in,
  input  [5:0] addr_set,
  output [7:0] bus_out,
  output [7:0] sd
);

  wire and_1_out, and_2_out, and_5_out, and_6_out, and_9_out, and_10_out, and_13_out, and_14_out,
       comparator_1_eq, decoder_1_out_0, decoder_1_out_1, decoder_1_out_2, decoder_1_out_3, decoder_1_out_4,
       decoder_1_out_5, decoder_1_out_6, decoder_1_out_7, ka_wtb, kb_wtb, register_1_p8, sd_rfb, sd_wtb,
       term_rfb;
  wire [0:0] uart_1_p5;
  wire [7:0] uart_1_p4;

  // register register_1: pin names not known; wires that end beside it: bus_in, clk, sd_rfb, sd_wtb, rset, 1'b0, 1'b0, register_1_p8, sd
  // Probe sd_peek on register_1_p8
  Comparator #(.Bits(3)) comparator_1 (.a(addr_in[5:3]), .b(addr_set[5:3]), .eq(comparator_1_eq));  // open: gt, lt
  Decoder #(.Selector_Bits(3)) decoder_1 (
    .sel(addr_in[2:0]), .out_0(decoder_1_out_0), .out_1(decoder_1_out_1), .out_2(decoder_1_out_2),
    .out_3(decoder_1_out_3), .out_4(decoder_1_out_4), .out_5(decoder_1_out_5), .out_6(decoder_1_out_6),
    .out_7(decoder_1_out_7));
  and and_1 (and_1_out, comparator_1_eq, decoder_1_out_0);
  and and_2 (and_2_out, decoder_1_out_7, comparator_1_eq);
  // uart uart_1: pin names not known; wires that end beside it: clk, term_rfb, bus_in, uart_1_p4, uart_1_p5[0]
  and and_3 (sd_rfb, rfb, and_1_out);
  and and_4 (sd_wtb, wtb, and_1_out);
  and and_5 (and_5_out, comparator_1_eq, decoder_1_out_1);
  and and_6 (and_6_out, decoder_1_out_6, comparator_1_eq);
  and and_7 (term_rfb, rfb, and_5_out);
  // And and_8 has open pins: In_1=wtb, In_2=and_5_out, out=open
  assign bus_out = kb_wtb ? uart_1_p4 : 8'bz;  // Driver driver_1
  assign bus_out = ka_wtb ? {{7{1'b0}}, uart_1_p5[0]} : 8'bz;  // Driver driver_2
  and and_9 (and_9_out, comparator_1_eq, decoder_1_out_2);
  and and_10 (and_10_out, decoder_1_out_5, comparator_1_eq);
  // And and_11 has open pins: In_1=rfb, In_2=and_9_out, out=open
  and and_12 (kb_wtb, wtb, and_9_out);
  and and_13 (and_13_out, comparator_1_eq, decoder_1_out_3);
  and and_14 (and_14_out, decoder_1_out_4, comparator_1_eq);
  // And and_15 has open pins: In_1=rfb, In_2=and_13_out, out=open
  and and_16 (ka_wtb, wtb, and_13_out);

  // Notes on the sheet:
  //   sd: Status Display
  //   Address plan:
  //   0x00 - status display (out/in)
  //   0x01 - terminal in
  //   0x02 - keyboard out
  //   0x03 - keyboard avail (
endmodule

/* Test case:
clk addr_set addr_in rfb wtb bus_in bus_out sd_peek
C   0x40     0x20     0   0   Z      Z      X
# put on SD and read it out
C   0x20     0x00     0   1   Z      Z      X
C   0x20     0x20     0   1   Z      X      0x00
C   0x20     0x20     1   0   0xff   Z      X
C   0x20     0x20     0   1   Z      X      0xff

# term tests (?)
C   0x20     0x21     1   0   0x22   Z      X

# kbd tests (?)
C   0x20     0x22     0   1   Z      0x00   X
C   0x20     0x23     0   1   Z      0x00   X
*/
