// Digital circuit pc_controller.dig as structural Verilog
module pc_controller (
  input  [2:0] PC_sel,
  input  [7:0] bus_in,
  input  [7:0] flags_in,
  input  clk,
  input  rset,
  input  cold_ena,
  output pcli,
  output pchi,
  output [7:0] pcl_bo,
  output [7:0] pch_bo
);

  wire and_1_out, and_2_out, bitselector_1_out, bitselector_2_out, counter_1_ovf, d_ff_1_nq,
       demultiplexer_1_out_0, demultiplexer_1_out_1, multiplexer_1_out, or_1_out, xor_1_out, xor_2_out;
  wire [1:0] counter_1_out;

  xor xor_1 (xor_1_out, counter_1_ovf, rset);
  and and_1 (and_1_out, d_ff_1_nq, clk);
  BitSelector #(.Selector_Bits(3)) bitselector_1 (.in(flags_in), .sel(3'b001), .out(bitselector_1_out));
  BitSelector #(.Selector_Bits(3)) bitselector_2 (.in(flags_in), .sel(3'b000), .out(bitselector_2_out));
  D_FF d_ff_1 (.D(counter_1_ovf), .C(xor_1_out), .nQ(d_ff_1_nq));  // open: Q
  or or_1 (or_1_out, and_1_out, rset);
  Counter #(.Bits(2)) counter_1 (.en(1'b1), .C(or_1_out), .clr(rset), .out(counter_1_out), .ovf(counter_1_ovf));
  xor xor_2 (xor_2_out, counter_1_out[0], counter_1_out[1]);
  Multiplexer #(.Selector_Bits(2)) multiplexer_1 (
    .sel(PC_sel[1:0]), .in_0(1'b0), .in_1(1'b1), .in_2(bitselector_1_out), .in_3(bitselector_2_out),
    .out(multiplexer_1_out));
  and and_2 (and_2_out, cold_ena, xor_2_out);
  Demultiplexer demultiplexer_1 (
    .sel(PC_sel[2]), .in(multiplexer_1_out), .out_0(demultiplexer_1_out_0), .out_1(demultiplexer_1_out_1));
  or or_2 (pchi, demultiplexer_1_out_1, and_2_out);
  or or_3 (pcli, demultiplexer_1_out_0, and_2_out);
  Multiplexer #(.Bits(8)) multiplexer_2 (.sel(and_2_out), .in_0(bus_in), .in_1(8'hfc), .out(pcl_bo));
  Multiplexer #(.Bits(8)) multiplexer_3 (.sel(and_2_out), .in_0(bus_in), .in_1({8{1'b1}}), .out(pch_bo));

  // Notes on the sheet:
  //   Equal/Zero
  //   Carry
  //   PC_SEL VALUES
  //   PCUU = 0b000 << 18 # PC Counters Unselected
  //   PLLU = 0b001 << 18 # PC Low in from bus, unconditional
  //   PLHU = 0b101 << 18 # PC Hi  in from bus, unconditional
  //   PLLE = 0b010 << 18 # PC Low in from bus, On Equal
  //   PLHE = 0b110 << 18 # PC Hi  in from bus, On Equal
  //   PLLC = 0b011 << 18 # PC Low in from bus, On Carry
  //   PLHC = 0b111 << 18 # PC Hi  in from bus, On Carry
  //   ----
  //   NV1B DIZC
endmodule

/* Test case Test Jumps:
clk PC_sel flags_in   pcli pchi bus_in pch_bo pcl_bo
# Not selected
C   0b000  0b00000000 0    0    X      X      X
C   0b100  0b00000000 0    0    X      X      X
# unconditional jump
C   0b001  0b00000000 1    0    X      X      X
C   0b101  0b00000000 0    1    X      X      X
# jump if equal
C   0b010  0b00000010 1    0    0x12   X      X
C   0b110  0b00000010 0    1    0x12   X      X
C   0b010  0b11111101 0    0    0x12   X      X
C   0b110  0b11111101 0    0    0x12   X      X
# jump if carry
C   0b011  0b00000001 1    0    X      X      X
C   0b111  0b00000001 0    1    X      X      X
C   0b111  0b11111110 0    0    X      X      X
*/

/* Test case Coldstart:
clk rset cold_ena bus_in pcl_bo pch_bo pcli pchi
# Cold start at PC startup
C   0    1        0x12      0xFC   0xFF   1    1
C   0    1        0x12      0xFC   0xFF   1    1
# C   0    1        Z      X      X      X    X
C   0    1        0x12      X       X    0    0
C   0    1        0x12      X       X    0    0
# Reset PC, should restart cold-start sequence
C   1    1        0x12      X       X    0    0
C   0    1        0x12      0xFC   0xFF   1    1
*/
